# Fritzing sketch circuit (saved by Fritzing 0.9.3b)
breadboards: 1

parts:
  부품1 = Arduino Uno (Rev3)
  LCM1602_IIC1 = LCM1602 IIC [part_number="LCM1602 IIC" chip_label="LCM1602 IIC" package="DIP (Dual Inline) [THT]"]
  Mod1 = gy-906

nets:
  N1: 부품1.A4/SDA, LCM1602_IIC1.SDA, Mod1.SDA
  N2: 부품1.A5/SCL, LCM1602_IIC1.SCL, Mod1.SCL
  5V: 부품1.5V, LCM1602_IIC1.VCC, Mod1.VIN
  GND: 부품1.GND, LCM1602_IIC1.GND, Mod1.GND

notes:
  VCC/VIN : 빨간색
  GND : 검정색

custom parts:
  LCM1602 IIC: I2C-Module to use a 1602 or 2004 LCD on with the wire.h libory Serial LCD Modul
  gy-906: gy-906 Non-contact PIR I2C interface temperature sensor breakout board.
